# Fritzing sketch RC_CAR_CONTROLLER (saved by Fritzing 0.9.3b)

parts:
  Part1 = Arduino Nano (Rev3.0)
  Part2 = 16-Channel 12-bit PCA9685 PWM/Servo Driver
  J1 = Basic Servo
  Part3 = Bluetooth HM-10
  BATT1 = LiPoly Battery (1300mAh)
  M3 = DC Motor  # not connected
  Part5 = MD13S
  Part6 = DC-DC Power Module (5v)
  Part7 = DC-DC Power Module (5v)
  Part8 = Adafruit DRV8871 [part_number="Adafruit #3190"]
  M4 = DC Motor
  R1 = Resistor [tolerance=±5% resistance=4.7k package=THT]  # not connected
  R2 = Resistor [tolerance=±5% resistance=6.8k package=THT]
  D1 = Diode [package=diode-1n4001]  # not connected
  U2 = LCD-16X2 [package=lcd-16x2_noholes]

nets:
  N1: Part1.D2, Part3.RXD
  N2: Part1.D3, Part3.TXD
  N3: Part1.D11/MOSI, Part8.IN2
  N4: Part1.VIN, Part6.Vout
  N5: Part1.A5, Part2.SCL, U2.VSS
  N6: Part1.A4, Part2.SDA, U2.VDD
  N7: Part1.A0, R2.Pin_1
  N8: Part2.0, J1.pulse
  VCC: Part2.V+, Part2.VCC, J1.vcc, Part7.Vout
  GND: Part2.GND, J1.gnd, Part7.GND*, U2.VO
  N9: BATT1.positive, Part5.no_name_yet#connector_N1
  N10: BATT1.negative, Part5.no_name_yet#connector_P1, Part6.GND, R2.Pin_0
  N11: Part8.OUT2, M4.pin_1
  N12: Part8.OUT1, M4.pin_2

custom parts:
  16-Channel 12-bit PCA9685 PWM/Servo Driver: The Adafruit 16-Channel 12-bit PWM/Servo Driver will drive up to 16 servos over I2C with only 2 pins. The on-board PCA9685 PWM controller will drive all 16 channels simultaneously with no additional processing overhead. What's more, you can chain up to 62 of them to control up to 992 servos - all with the same 2 pins
  LiPoly Battery (1300mAh): Lithium Ion Polymer Battery (1300mAh)
  DC-DC Power Module (5v): DC-DC Power Module based con AMS1117-5.0 Input: DC 6~12V (input power must higher 1V than output power); Output: 5V (+/-0.05V error), 800mA
  Adafruit DRV8871: Crank up your robotics with powerful Adafruit DRV8871 motor driver breakout board. This motor driver has a lot of great specs that make it useful for a wide variety of mechatronics. In particular, the simple resistor-set current limiting and auto-magic PWM support make it super easy to use. Check out the specs for the DRV8871: 6.5V to 45V motor power voltage Up to 5.5V logic level on IN pins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
